# Fritzing sketch MCP9808_FeatherM0Adalogger (saved by Fritzing 0.7.5b)
breadboards: 1

parts:
  Part1 = Adafruit Feather M0 Adalogger [part_number="Adafruit #2796"]
  Part2 = MCP9808 High Accuracy I2C Temperature Sensor [part_number=1782]

nets:
  GND: Part1.GND, Part2.GND
  +3V3: Part1.+3V3, Part2.VDD
  N1: Part1.D5, Part2.ALERT
  N2: Part1.SCL, Part2.SCL
  N3: Part1.SDA, Part2.SDA

custom parts:
  Adafruit Feather M0 Adalogger: This is the Adafruit Feather M0 Adalogger - our take on an 'all-in-one' Cortex M0 datalogger (or data-reader) with built in USB and battery charging. Its an Adafruit Feather M0 with a microSD holder ready to rock! We have other boards in the Feather family, check'em out here At the Feather M0's heart is an ATSAMD21G18 ARM Cortex M0 processor, clocked at 48 MHz and at 3.3V logic, the same one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
  MCP9808 High Accuracy I2C Temperature Sensor: This I2C digital temperature sensor is one of the more accurate/precise we've ever seen, with a typical accuracy of ±0.25°C over the sensor's -40°C to +125°C range and precision of +0.0625°C. They work great with any microcontroller using standard i2c. There are 3 address pins so you can connect up to 8 to a single I2C bus without address collisions. Best of all, a wide voltage range makes is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
